# Fritzing sketch ArDe_v1.0 (saved by Fritzing 0.8.5b)
breadboards: 1

parts:
  Componente1 = Arduino Uno (Rev3)
  LCD1 = LCD screen
  R1 = Trimmer Potentiometer [maximum_resistance=10kΩ package=THT]
  R2 = Resistor [tolerance=±5% resistance=10k package=THT]
  R3 = Resistor [tolerance=±5% resistance=220 package=THT]
  R4 = Photocell (LDR) [package=THT]
  LED1 = LED - 5mm [color="Red (633nm)" package="5 mm [THT]"]
  R5 = Resistor [tolerance=±5% resistance=220 package=THT]
  R6 = Resistor [tolerance=±5% resistance=220 package=THT]
  LED2 = LED - 5mm [color="Green (555nm)" package="5 mm [THT]"]
  J1 = Piezo Speaker
  R7 = Resistor [tolerance=±5% resistance=220 package=THT]

nets:
  N1: Componente1.A0, R3.Pin_1, R4.pin_0
  N2: Componente1.D8, LED2.anode
  N3: Componente1.D9_PWM, LED1.anode
  N4: Componente1.D11_PWM/MOSI, LCD1.E
  N5: Componente1.D12/MISO, LCD1.RS
  GND: Componente1.GND, LCD1.VSS, LCD1.R/W, LCD1.LED-, R1.leg2, R3.Pin_0, R5.Pin_0, R6.Pin_0, R7.Pin_1
  N6: Componente1.D2, LCD1.DB7
  N7: Componente1.D3_PWM, LCD1.DB6
  N8: Componente1.D4, LCD1.DB5
  N9: Componente1.D5_PWM, LCD1.DB4
  N10: Componente1.D6_PWM, J1.pin2
  5V: Componente1.5V, LCD1.VDD, R1.leg1, R2.Pin_0, R4.pin_1
  N11: LCD1.V0, R1.wiper
  N12: LCD1.LED+, R2.Pin_1
  N13: LED1.cathode, R5.Pin_1
  N14: R6.Pin_1, LED2.cathode

notes:
  //
  // Coded By Marco Angione
  // @marc_angio on twitter & GitHub
  //
  You need to point a laser towards the photocell
